# Fritzing sketch Untitled Sketch 2.jpg (saved by Fritzing 0.9.3b)
breadboards: 1

parts:
  Composant1 = ESP-WROOM-32 [ESP-32S] Module [part_number=ESP-WROOM-32]
  hc-sr1 = hc-sr04

nets:
  GND: Composant1.GND, hc-sr1.GND
  3V3: Composant1.3V3, hc-sr1.VCC
  N1: Composant1.IO5, hc-sr1.Trig
  N2: Composant1.IO18, hc-sr1.Echo

custom parts:
  ESP-WROOM-32 [ESP-32S] Module: Espressif ESP-WROOM-32 WiFi/Bluetooth LE microcontroller module also known as the Ai-Thinker ESP-32S module with similar formfactor. The ESP32 is a microcontroller chip with WiFi and BLE capabilities. The chip is developed by Espressif and is the successor to the popular ESP8266 WiFi module.
